# Fritzing sketch ColorPickerSchem (saved by Fritzing 0.9.3b)
breadboards: 1

parts:
  Part1 = Arduino Uno (Rev3)
  S1 = Momentary Switch [package=ksa_sealed_tac_switch]
  LED1 = RGB LED (com. cathode, rgb) [package="5 mm [THT]"]
  R1 = Resistor [tolerance=±5% resistance=220 package=THT]
  R2 = Resistor [tolerance=±5% resistance=220 package=THT]
  R3 = Resistor [tolerance=±5% resistance=220 package=THT]

nets:
  N1: Part1.D9_PWM, R3.Pin_1
  N2: Part1.D10_PWM/SS, R2.Pin_1
  N3: Part1.D11_PWM/MOSI, R1.Pin_1
  N4: Part1.GND, S1.1, LED1.green_anode
  N5: Part1.D2, S1.3
  N6: LED1.red_anode, R1.Pin_0
  N7: LED1.common_cathode, R2.Pin_0
  N8: LED1.blue_anode, R3.Pin_0

notes:
  Button starts and stops light.
